# Fritzing sketch Traffic_Lights_Wiring_Diagram (saved by Fritzing 0.9.10b)
breadboards: 1

parts:
  Part1 = Arduino Mega 2560 (Rev3)
  S1 = Pushbutton [package="[THT]"]
  S2 = Pushbutton [package="[THT]"]
  R1 = Resistor [tolerance=±5% power=0.25 resistance=10k package=THT]
  LED1 = LED - 5mm [color="Red (633nm)" current=0.030 package="5 mm [THT]"]
  LED2 = LED - 5mm [color="Red (633nm)" current=0.030 package="5 mm [THT]"]
  LED3 = LED - 5mm [color="Orange (612nm)" current=0.030 package="5 mm [THT]"]
  LED4 = LED - 5mm [color="Green (565nm)" current=0.030 package="5 mm [THT]"]
  LED5 = LED - 5mm [color="Orange (612nm)" current=0.030 package="5 mm [THT]"]
  LED6 = LED - 5mm [color="Green (565nm)" current=0.030 package="5 mm [THT]"]
  R2 = Resistor [tolerance=±5% power=0.25 resistance=220 package=THT]
  R3 = Resistor [tolerance=±5% power=0.25 resistance=220 package=THT]
  R4 = Resistor [tolerance=±5% power=0.25 resistance=220 package=THT]
  R5 = Resistor [tolerance=±5% power=0.25 resistance=220 package=THT]
  R6 = Resistor [tolerance=±5% power=0.25 resistance=220 package=THT]
  R7 = Resistor [tolerance=±5% power=0.25 resistance=330 package=THT]

nets:
  N1: Part1.GND, Part1.D8_PWM, R1.Pin_0, LED1.anode, LED2.anode, LED3.anode, LED4.anode, LED5.anode, LED6.anode
  N2: Part1.D12_PWM, R7.Pin_0
  N3: Part1.D11_PWM, R6.Pin_0
  N4: Part1.D10_PWM, R5.Pin_0
  N5: Part1.5V, S1.Pin_1, S1.Pin_2, S2.Pin_1, S2.Pin_2
  N6: S1.Pin_3, S1.Pin_4, S2.Pin_3, S2.Pin_4, R1.Pin_1
  N7: LED1.cathode, R7.Pin_1
  N8: LED2.cathode, R2.Pin_1
  N9: LED3.cathode, R3.Pin_1
  N10: LED4.cathode, R4.Pin_1
  N11: LED5.cathode, R6.Pin_1
  N12: LED6.cathode, R5.Pin_1

// code stored in the sketch: Traffic_Lights_Wiring_Diagram.fzz.ino
// Digital pin 8 has a pushbutton attached to it. Assign the name pushButton:
int pushButton = 8;

// Digital pin 12 has a red LED attached to it. Assign the name RedLED:
int RedLED = 12 ;

// Digital pin 11 has an amber LED attached to it. Assign the name AmberLED:
int AmberLED = 11;

// Digital pin 10 has a green LED attached to it. Assign the name GreenLED:
int GreenLED = 10;

// The setup routine runs once when you press reset:
void setup() {

// Initialize serial communication at 9600 bits per second:
Serial.begin(9600);
  
// Assign the pushbutton's pin an input:
  pinMode(pushButton, INPUT);
  
// Assign the LEDs pins as outputs:  
  pinMode(RedLED,OUTPUT);
  pinMode(AmberLED,OUTPUT);
  pinMode(GreenLED, OUTPUT);

// Initialise the LED states so that traffic can flow with just the green LED illuminated.
digitalWrite(RedLED,LOW);
digitalWrite(AmberLED,LOW);
digitalWrite(GreenLED,HIGH);
}

// the loop routine runs over and over again forever:
void loop() {
  // read the input pin:
  int buttonState = digitalRead(pushButton);
  // print out the state of the button only if the button is being pressed:
  if (buttonState==HIGH)
  {
    delay(1000);
    digitalWrite(GreenLED,LOW);
    digitalWrite(AmberLED,HIGH);
    delay(3000);
    digitalWrite(AmberLED,LOW);
    digitalWrite(RedLED,HIGH);
    delay(6000);
    digitalWrite(AmberLED,HIGH);
    delay(1500);
    digitalWrite(RedLED,LOW);
    digitalWrite(AmberLED,LOW);
    Serial.print (" Pushbutton is pressed, value is :");
  Serial.println(buttonState);
  }
  else
  {
    digitalWrite(GreenLED,HIGH);
  }
  delay(1);        // delay in between reads for stability
}
